// Logisim project project final.circ as structural Verilog: 1 circuit, main circuit main
module main (
  input  A3,
  input  A2,
  input  A1,
  input  A0,
  input  B3,
  input  B2,
  input  B1,
  input  B0,
  input  in_9,
  input  in_10,
  input  in_11,
  input  in_12,
  input  in_13,
  input  in_14,
  input  in_15,
  input  in_16,
  input  in_17,
  input  in_18,
  input  in_19,
  input  [2:0] in_20,
  input  in_21,
  output out_22,
  output out_23,
  output out_24,
  output out_25,
  output C3,
  output C2,
  output C1,
  output C0
);

  wire adder_1_cout, adder_1_out, adder_2_cout, adder_2_out, adder_3_cout, adder_3_out, adder_4_out,
       adder_5_cout, adder_5_out, adder_6_cout, adder_6_out, adder_7_cout, adder_7_out, adder_8_cout,
       adder_8_out, adder_9_cout, adder_9_out, adder_10_cout, adder_10_out, adder_11_cout, adder_11_out,
       adder_12_cout, adder_12_out, adder_13_cout, adder_13_out, adder_14_cout, adder_14_out, adder_15_cout,
       adder_15_out, adder_16_cout, adder_16_out, adder_17_cout, adder_17_out, adder_18_cout, adder_18_out,
       adder_19_cout, adder_19_out, adder_20_cout, adder_20_out, adder_21_cout, adder_21_out, adder_22_cout,
       adder_22_out, adder_23_cout, adder_23_out, adder_24_cout, adder_24_out, and_1_out, and_2_out,
       and_3_out, and_4_out, and_5_out, and_6_out, and_7_out, and_8_out, and_9_out, and_10_out, and_11_out,
       and_12_out, and_13_out, and_14_out, and_15_out, and_16_out, nand_1_out, nand_2_out, nand_3_out,
       nand_4_out, not_1_out, not_2_out, not_3_out, not_4_out, or_1_out, or_2_out, or_3_out, or_4_out,
       xor_1_out, xor_2_out, xor_3_out, xor_4_out;

  and and_1 (and_1_out, A3, B3);
  and and_2 (and_2_out, A2, B3);
  and and_3 (and_3_out, A3, B2);
  Adder #(.width(1)) adder_1 (.a(and_3_out), .b(and_2_out), .out(adder_1_out), .cin(in_15), .cout(adder_1_cout));
  Adder #(.width(1)) adder_2 (
    .a(and_1_out), .b(adder_1_cout), .out(adder_2_out), .cin(adder_3_cout), .cout(adder_2_cout));
  and and_4 (and_4_out, B3, A1);
  Adder #(.width(1)) adder_3 (
    .a(adder_6_cout), .b(adder_7_cout), .out(adder_3_out), .cin(adder_1_out), .cout(adder_3_cout));
  Multiplexer #(.select(3)) multiplexer_1 (
    .in0(in_19), .in1(in_19), .in2(in_19), .in3(adder_2_cout), .in4(in_19), .in5(in_19), .in6(in_19),
    .in7(in_19), .out(out_22), .sel(in_20));  // open: en
  and and_5 (and_5_out, A3, B1);
  and and_6 (and_6_out, A2, B2);
  and and_7 (and_7_out, A2, B1);
  Adder #(.width(1)) adder_4 (.a(and_6_out), .b(and_5_out), .out(adder_4_out), .cin(adder_5_cout), .cout(in_15));
  Multiplexer #(.select(3)) multiplexer_2 (
    .in0(in_19), .in1(in_19), .in2(in_19), .in3(adder_2_out), .in4(in_19), .in5(in_19), .in6(in_19),
    .in7(in_19), .out(out_23), .sel(in_20));  // open: en
  and and_8 (and_8_out, A3, B0);
  Adder #(.width(1)) adder_5 (.a(and_8_out), .b(and_7_out), .out(adder_5_out), .cin(in_16), .cout(adder_5_cout));
  Adder #(.width(1)) adder_6 (
    .a(and_4_out), .b(adder_4_out), .out(adder_6_out), .cin(adder_8_cout), .cout(adder_6_cout));
  and and_9 (and_9_out, A0, B3);
  Adder #(.width(1)) adder_7 (.a(adder_9_cout), .b(adder_6_out), .out(adder_7_out), .cin(in_16), .cout(adder_7_cout));
  and and_10 (and_10_out, A1, B2);
  and and_11 (and_11_out, A1, B1);
  Adder #(.width(1)) adder_8 (
    .a(and_10_out), .b(adder_5_out), .out(adder_8_out), .cin(adder_10_cout), .cout(adder_8_cout));
  Multiplexer #(.select(3)) multiplexer_3 (
    .in0(in_19), .in1(in_19), .in2(in_19), .in3(adder_3_out), .in4(in_19), .in5(in_19), .in6(in_19),
    .in7(in_19), .out(out_24), .sel(in_20));  // open: en
  and and_12 (and_12_out, A2, B0);
  Adder #(.width(1)) adder_9 (
    .a(adder_8_out), .b(and_9_out), .out(adder_9_out), .cin(adder_11_cout), .cout(adder_9_cout));
  and and_13 (and_13_out, A0, B2);
  Adder #(.width(1)) adder_10 (.a(and_12_out), .b(and_11_out), .out(adder_10_out), .cin(in_17), .cout(adder_10_cout));
  Multiplexer #(.select(3)) multiplexer_4 (
    .in0(in_19), .in1(in_19), .in2(in_19), .in3(adder_7_out), .in4(adder_13_cout), .in5(adder_17_cout),
    .in6(adder_21_cout), .in7(in_19), .out(out_25), .sel(in_20));  // open: en
  and and_14 (and_14_out, A1, B0);
  and and_15 (and_15_out, A0, B1);
  Adder #(.width(1)) adder_11 (
    .a(and_13_out), .b(adder_10_out), .out(adder_11_out), .cin(adder_12_cout), .cout(adder_11_cout));
  and and_16 (and_16_out, A0, B0);
  Adder #(.width(1)) adder_12 (.a(and_15_out), .b(and_14_out), .out(adder_12_out), .cin(in_14), .cout(adder_12_cout));
  Multiplexer #(.select(3)) multiplexer_5 (
    .in0(or_1_out), .in1(nand_1_out), .in2(xor_1_out), .in3(adder_9_out), .in4(adder_13_out),
    .in5(adder_17_out), .in6(adder_21_out), .in7(in_21), .out(C3), .sel(in_20));  // open: en
  Adder #(.width(1)) adder_13 (.a(A3), .b(B3), .out(adder_13_out), .cin(adder_14_cout), .cout(adder_13_cout));
  Adder #(.width(1)) adder_14 (.a(A2), .b(B2), .out(adder_14_out), .cin(adder_15_cout), .cout(adder_14_cout));
  Multiplexer #(.select(3)) multiplexer_6 (
    .in0(or_2_out), .in1(nand_2_out), .in2(xor_2_out), .in3(adder_11_out), .in4(adder_14_out),
    .in5(adder_18_out), .in6(adder_22_out), .in7(A3), .out(C2), .sel(in_20));  // open: en
  Adder #(.width(1)) adder_15 (.a(A1), .b(B1), .out(adder_15_out), .cin(adder_16_cout), .cout(adder_15_cout));
  nand nand_1 (nand_1_out, A3, B3);
  Adder #(.width(1)) adder_16 (.a(A0), .b(B0), .out(adder_16_out), .cout(adder_16_cout));  // open: cin
  nand nand_2 (nand_2_out, A2, B2);
  Multiplexer #(.select(3)) multiplexer_7 (
    .in0(or_3_out), .in1(nand_3_out), .in2(xor_3_out), .in3(adder_12_out), .in4(adder_15_out),
    .in5(adder_19_out), .in6(adder_23_out), .in7(A2), .out(C1), .sel(in_20));  // open: en
  nand nand_3 (nand_3_out, A1, B1);
  nand nand_4 (nand_4_out, A0, B0);
  or or_1 (or_1_out, A3, A3, B3, B3);
  or or_2 (or_2_out, A2, A2, B2, B2);
  Multiplexer #(.select(3)) multiplexer_8 (
    .in0(or_4_out), .in1(nand_4_out), .in2(xor_4_out), .in3(and_16_out), .in4(adder_16_out),
    .in5(adder_20_out), .in6(adder_24_out), .in7(A1), .out(C0), .sel(in_20));  // open: en
  or or_3 (or_3_out, A1, A1, B1, B1);
  or or_4 (or_4_out, A0, A0, B0, B0);
  ExactlyOne xor_1 (.out(xor_1_out), .in0(A3), .in1(A3), .in3(B3), .in4(B3));
  ExactlyOne xor_2 (.out(xor_2_out), .in0(A2), .in1(A2), .in3(B2), .in4(B2));
  ExactlyOne xor_3 (.out(xor_3_out), .in0(A1), .in1(A1), .in3(B1), .in4(B1));
  ExactlyOne xor_4 (.out(xor_4_out), .in0(A0), .in1(A0), .in3(B0), .in4(B0));
  Adder #(.width(1)) adder_17 (.a(A3), .b(adder_18_cout), .out(adder_17_out), .cin(in_10), .cout(adder_17_cout));
  Adder #(.width(1)) adder_18 (.a(A2), .b(adder_19_cout), .out(adder_18_out), .cin(in_11), .cout(adder_18_cout));
  Adder #(.width(1)) adder_19 (.a(A1), .b(adder_20_cout), .out(adder_19_out), .cin(in_12), .cout(adder_19_cout));
  not not_1 (not_1_out, B3);
  Adder #(.width(1)) adder_20 (.a(A0), .b(in_18), .out(adder_20_out), .cin(in_13), .cout(adder_20_cout));
  not not_2 (not_2_out, B2);
  Adder #(.width(1)) adder_21 (.a(A3), .b(not_1_out), .out(adder_21_out), .cin(adder_22_cout), .cout(adder_21_cout));
  not not_3 (not_3_out, B1);
  Adder #(.width(1)) adder_22 (.a(A2), .b(not_2_out), .out(adder_22_out), .cin(adder_23_cout), .cout(adder_22_cout));
  not not_4 (not_4_out, B0);
  Adder #(.width(1)) adder_23 (.a(A1), .b(not_3_out), .out(adder_23_out), .cin(adder_24_cout), .cout(adder_23_cout));
  Adder #(.width(1)) adder_24 (.a(A0), .b(not_4_out), .out(adder_24_out), .cin(in_9), .cout(adder_24_cout));
endmodule
